# Fritzing sketch Lesson02_Button (saved by Fritzing 0.9.2b)
breadboards: 1

parts:
  LED1 = LED - 5mm [color="Blue (505nm)" package="5 mm [THT]"]
  Raspberry_Pi1 = Raspberry Pi 2
  S1 = Momentary Switch [package=ksa_sealed_tac_switch]
  R1 = Resistor [tolerance=±5% resistance=220 package="0603 [SMD]"]
  R2 = Resistor [tolerance=±5% resistance=6.8k package="2512 [SMD]"]

nets:
  N1: LED1.cathode, R1.Pin_1
  N2: LED1.anode, Raspberry_Pi1.GPIO25
  N3: Raspberry_Pi1.3v3, S1.4
  N4: Raspberry_Pi1.GPIO24, S1.1
  N5: Raspberry_Pi1.GND, R1.Pin_0, R2.Pin_1
  N6: S1.2, R2.Pin_0
